// Digital circuit Negation3.dig as structural Verilog
// 3-bit unsigned to 4-bit two's complement negation: -X = ~X + 1.
// 先把 3 位零扩展到 4 位，按位取反，再用习题 1 的 4 位后继器加 1。
module Negation3 (
  input  X_0,
  input  X_1,
  input  X_2,
  output Y_0,
  output Y_1,
  output Y_2,
  output Y_3
);

  wire not_1_out, not_2_out, not_3_out, not_4_out;

  not not_1 (not_1_out, X_0);
  not not_2 (not_2_out, X_1);
  not not_3 (not_3_out, X_2);
  not not_4 (not_4_out, 1'b0);
  Successor4 successor4_1 (
    .A_0(not_1_out), .S_0(Y_0), .A_1(not_2_out), .A_2(not_3_out), .A_3(not_4_out), .S_1(Y_1), .S_2(Y_2),
    .S_3(Y_3));  // open: C_out

  // Notes on the sheet:
  //   X_0: LSB of the unsigned 3-bit input
  //   X_1: Input bit 1
  //   X_2: MSB of the unsigned 3-bit input
  //   Y_0: LSB of -X in 4-bit two's complement
  //   Y_3: Sign bit of -X
  //   Exercise 2  3-bit negation to 4-bit two's complement  -X = ~X + 1
  //   invert 4-bit zero-extend
  //   then +1  (Exercise 1 successor)
endmodule

/* Test case all-8-inputs:
# All 8 inputs. Y is the 4-bit two's complement of -X.
# 001 -> 1111 (-1); 010 -> 1110 (-2); 000 -> 0000; 111 -> 1001 (-7).
X_2 X_1 X_0 Y_3 Y_2 Y_1 Y_0
loop(n,8)
bits(3,n) bits(4,16-n)
end loop
*/
